// Logisim project 7_segmentos.circ as structural Verilog: 1 circuit, main circuit 7 segmentos
module _7_segmentos (
  input  D,
  input  C,
  input  B,
  input  A,
  output a_2,
  output b_2,
  output c_2,
  output d_2,
  output e,
  output f,
  output g
);

  wire and_1_out, and_2_out, and_3_out, and_4_out, and_5_out, and_6_out, and_7_out, and_8_out, and_9_out,
       and_10_out, and_11_out, and_12_out, and_13_out, and_14_out, and_15_out, and_16_out;

  and and_1 (and_1_out, B, ~C);  // AND_Gate
  and and_2 (and_2_out, ~B, C);  // AND_Gate
  and and_3 (and_3_out, B, ~D);  // AND_Gate
  and and_4 (and_4_out, ~C, ~D);  // AND_Gate
  and and_5 (and_5_out, B, ~D);  // AND_Gate
  and and_6 (and_6_out, B, ~C);  // AND_Gate
  and and_7 (and_7_out, ~B, ~D);  // AND_Gate
  and and_8 (and_8_out, B, D);
  and and_9 (and_9_out, ~C, ~D);  // AND_Gate
  and and_10 (and_10_out, C, D);
  and and_11 (and_11_out, ~B, ~D);  // AND_Gate
  and and_12 (and_12_out, C, ~D);  // AND_Gate
  and and_13 (and_13_out, ~B, ~D);  // AND_Gate
  and and_14 (and_14_out, C, ~D);  // AND_Gate
  and and_15 (and_15_out, B, ~C, D);  // AND_Gate
  and and_16 (and_16_out, ~B, C);  // AND_Gate
  or or_1 (a_2, and_1_out, A, and_2_out, and_3_out);
  or or_2 (b_2, and_4_out, A, and_5_out, and_6_out);
  or or_3 (c_2, and_7_out, A, C, and_8_out);
  or or_4 (d_2, and_9_out, ~B, and_10_out);  // OR_Gate
  or or_5 (e, and_11_out, and_12_out);
  or or_6 (f, and_13_out, and_14_out, and_15_out, and_16_out);
  or or_7 (g, B, ~C, D);  // OR_Gate
endmodule
