// Logisim project Contador-2-Horas.circ as structural Verilog: 1 circuit, main circuit Contador-2-Horas
module Contador_2_Horas (
  output a,
  output b,
  output c,
  output d,
  output e,
  output f,
  output g,
  output _24,
  output reset
);

  wire and_1_out, and_2_out, and_3_out, contador_6_minutos_1_reset, contador_6_minutos_2_reset, j_k_ff_1_q,
       j_k_ff_2_q, j_k_ff_3_q, j_k_ff_4_q, j_k_ff_5_q, j_k_ff_6_q, j_k_ff_7_q, j_k_ff_8_q, j_k_ff_9_q,
       j_k_ff_10_q, j_k_ff_11_q, j_k_ff_12_q, j_k_ff_13_q, or_1_out, s_r_ff_1_q;

  Contador_6_Minutos contador_6_minutos_1 (.reset(contador_6_minutos_1_reset));  // open: a, b, c, d, e, f, g
  or or_1 (or_1_out, _24, and_1_out);
  and and_1 (and_1_out, ~j_k_ff_1_q, j_k_ff_2_q, ~j_k_ff_5_q, j_k_ff_6_q);  // AND_Gate
  J_K_Flip_Flop #(.trigger("falling")) j_k_ff_1 (
    .J(1'b1), .clk(contador_6_minutos_1_reset), .K(1'b1), .Q(j_k_ff_1_q), .reset(or_1_out));  // open: Qn, preset, en
  J_K_Flip_Flop #(.trigger("falling")) j_k_ff_2 (
    .J(1'b1), .clk(j_k_ff_1_q), .K(1'b1), .Q(j_k_ff_2_q), .reset(or_1_out));  // open: Qn, preset, en
  J_K_Flip_Flop j_k_ff_3 (.J(1'b1), .clk(and_1_out), .K(1'b1), .Q(j_k_ff_3_q), .reset(_24));  // open: Qn, preset, en
  J_K_Flip_Flop #(.trigger("falling")) j_k_ff_4 (
    .J(1'b1), .clk(j_k_ff_3_q), .K(1'b1), .Q(j_k_ff_4_q), .reset(_24));  // open: Qn, preset, en
  J_K_Flip_Flop #(.trigger("falling")) j_k_ff_5 (
    .J(1'b1), .clk(j_k_ff_2_q), .K(1'b1), .Q(j_k_ff_5_q), .reset(or_1_out));  // open: Qn, preset, en
  J_K_Flip_Flop #(.trigger("falling")) j_k_ff_6 (
    .J(1'b1), .clk(j_k_ff_5_q), .K(1'b1), .Q(j_k_ff_6_q), .reset(or_1_out));  // open: Qn, preset, en
  J_K_Flip_Flop #(.trigger("falling")) j_k_ff_7 (
    .J(1'b1), .clk(j_k_ff_4_q), .K(1'b1), .Q(j_k_ff_7_q), .reset(_24));  // open: Qn, preset, en
  _7_segmentos u_7_segmentos_1 (
    .D(j_k_ff_3_q), .C(j_k_ff_4_q), .B(j_k_ff_7_q), .A(1'b0), .a_2(a), .b_2(b), .c_2(c), .d_2(d), .e(e),
    .f(f), .g(g));
  and and_2 (and_2_out, ~j_k_ff_8_q, j_k_ff_9_q, ~j_k_ff_11_q);  // AND_Gate
  Contador_6_Minutos contador_6_minutos_2 (.reset(contador_6_minutos_2_reset));  // open: a, b, c, d, e, f, g
  S_R_Flip_Flop #(.trigger("high")) s_r_ff_1 (
    .S(and_2_out), .clk(1'b1), .R(1'b0), .Q(s_r_ff_1_q), .reset(_24));  // open: Qn, preset, en
  J_K_Flip_Flop j_k_ff_8 (
    .J(1'b1), .clk(and_1_out), .K(1'b1), .Q(j_k_ff_8_q), .reset(and_2_out));  // open: Qn, preset, en
  and and_3 (and_3_out, contador_6_minutos_2_reset, s_r_ff_1_q);
  J_K_Flip_Flop #(.trigger("falling")) j_k_ff_9 (
    .J(1'b1), .clk(j_k_ff_8_q), .K(1'b1), .Q(j_k_ff_9_q), .reset(and_2_out));  // open: Qn, preset, en
  and and_4 (_24, ~j_k_ff_10_q, ~j_k_ff_12_q, j_k_ff_13_q);  // AND_Gate
  J_K_Flip_Flop #(.trigger("falling")) j_k_ff_10 (
    .J(1'b1), .clk(and_3_out), .K(1'b1), .Q(j_k_ff_10_q), .reset(_24));  // open: Qn, preset, en
  J_K_Flip_Flop #(.trigger("falling")) j_k_ff_11 (
    .J(1'b1), .clk(j_k_ff_9_q), .K(1'b1), .Q(j_k_ff_11_q), .reset(and_2_out));  // open: Qn, preset, en
  J_K_Flip_Flop #(.trigger("falling")) j_k_ff_12 (
    .J(1'b1), .clk(j_k_ff_10_q), .K(1'b1), .Q(j_k_ff_12_q), .reset(_24));  // open: Qn, preset, en
  J_K_Flip_Flop #(.trigger("falling")) j_k_ff_13 (
    .J(1'b1), .clk(j_k_ff_12_q), .K(1'b1), .Q(j_k_ff_13_q), .reset(_24));  // open: Qn, preset, en

  assign reset = _24;

  // Notes on the sheet:
  //   Contador 9
  //   Contador 2 Horas
  //   D
  //   C
  //   B
  //   A
  //   Contador 2
  //   Contador 4
endmodule
