// Logisim project Contador-6-Segundos.circ as structural Verilog: 1 circuit, main circuit Contador-6-Segundos
module Contador_6_Segundos (
  output a,
  output b,
  output c,
  output d,
  output e,
  output f,
  output g,
  output reset
);

  wire contador_9_segundos_1_reset, j_k_ff_1_q, j_k_ff_2_q, j_k_ff_3_q;

  Contador_9_Segundos contador_9_segundos_1 (.reset(contador_9_segundos_1_reset));  // open: a, b, c, d, e, f, g
  J_K_Flip_Flop j_k_ff_1 (
    .J(1'b1), .clk(contador_9_segundos_1_reset), .K(1'b1), .Q(j_k_ff_1_q), .reset(reset));  // open: Qn, preset, en
  and and_1 (reset, ~j_k_ff_1_q, j_k_ff_2_q, j_k_ff_3_q);  // AND_Gate
  J_K_Flip_Flop #(.trigger("falling")) j_k_ff_2 (
    .J(1'b1), .clk(j_k_ff_1_q), .K(1'b1), .Q(j_k_ff_2_q), .reset(reset));  // open: Qn, preset, en
  J_K_Flip_Flop #(.trigger("falling")) j_k_ff_3 (
    .J(1'b1), .clk(j_k_ff_2_q), .K(1'b1), .Q(j_k_ff_3_q), .reset(reset));  // open: Qn, preset, en
  _7_segmentos u_7_segmentos_1 (
    .D(j_k_ff_1_q), .C(j_k_ff_2_q), .B(j_k_ff_3_q), .A(1'b0), .a_2(a), .b_2(b), .c_2(c), .d_2(d), .e(e),
    .f(f), .g(g));

  // Notes on the sheet:
  //   D
  //   C
  //   B
  //   A
endmodule
