// Logisim project Contador-9-Segundos.circ as structural Verilog: 1 circuit, main circuit Contador-9-Segundos
module Contador_9_Segundos (
  output a,
  output b,
  output c,
  output d,
  output e,
  output f,
  output g,
  output reset
);

  wire clock_1_out, j_k_ff_1_q, j_k_ff_2_q, j_k_ff_3_q, j_k_ff_4_q;

  Clock clock_1 (.out(clock_1_out));
  and and_1 (reset, ~j_k_ff_1_q, j_k_ff_2_q, ~j_k_ff_3_q, j_k_ff_4_q);  // AND_Gate
  J_K_Flip_Flop #(.trigger("falling")) j_k_ff_1 (
    .J(1'b1), .clk(clock_1_out), .K(1'b1), .Q(j_k_ff_1_q), .reset(reset));  // open: Qn, preset, en
  J_K_Flip_Flop #(.trigger("falling")) j_k_ff_2 (
    .J(1'b1), .clk(j_k_ff_1_q), .K(1'b1), .Q(j_k_ff_2_q), .reset(reset));  // open: Qn, preset, en
  J_K_Flip_Flop #(.trigger("falling")) j_k_ff_3 (
    .J(1'b1), .clk(j_k_ff_2_q), .K(1'b1), .Q(j_k_ff_3_q), .reset(reset));  // open: Qn, preset, en
  _7_segmentos u_7_segmentos_1 (
    .D(j_k_ff_1_q), .C(j_k_ff_2_q), .B(j_k_ff_3_q), .A(j_k_ff_4_q), .a_2(a), .b_2(b), .c_2(c), .d_2(d),
    .e(e), .f(f), .g(g));
  J_K_Flip_Flop #(.trigger("falling")) j_k_ff_4 (
    .J(1'b1), .clk(j_k_ff_3_q), .K(1'b1), .Q(j_k_ff_4_q), .reset(reset));  // open: Qn, preset, en

  // Notes on the sheet:
  //   D
  //   C
  //   B
  //   A
endmodule
