// Logisim project Contador-Horas-Unidade.circ as structural Verilog: 1 circuit, main circuit Contador-Horas-Unidade
module Contador_Horas_Unidade (
  output a,
  output b,
  output c,
  output d,
  output e,
  output f,
  output g,
  output reset
);

  wire contador_2_horas_1__24, contador_6_minutos_1_reset, j_k_ff_1_q, j_k_ff_2_q, j_k_ff_3_q, j_k_ff_4_q,
       or_1_out;

  Contador_6_Minutos contador_6_minutos_1 (.reset(contador_6_minutos_1_reset));  // open: a, b, c, d, e, f, g
  or or_1 (or_1_out, contador_2_horas_1__24, reset);
  Contador_2_Horas contador_2_horas_1 (._24(contador_2_horas_1__24));  // open: a, b, c, d, e, f, g, reset
  and and_1 (reset, ~j_k_ff_1_q, j_k_ff_2_q, ~j_k_ff_3_q, j_k_ff_4_q);  // AND_Gate
  J_K_Flip_Flop #(.trigger("falling")) j_k_ff_1 (
    .J(1'b1), .clk(contador_6_minutos_1_reset), .K(1'b1), .Q(j_k_ff_1_q), .reset(or_1_out));  // open: Qn, preset, en
  J_K_Flip_Flop #(.trigger("falling")) j_k_ff_2 (
    .J(1'b1), .clk(j_k_ff_1_q), .K(1'b1), .Q(j_k_ff_2_q), .reset(or_1_out));  // open: Qn, preset, en
  J_K_Flip_Flop #(.trigger("falling")) j_k_ff_3 (
    .J(1'b1), .clk(j_k_ff_2_q), .K(1'b1), .Q(j_k_ff_3_q), .reset(or_1_out));  // open: Qn, preset, en
  _7_segmentos u_7_segmentos_1 (
    .D(j_k_ff_1_q), .C(j_k_ff_2_q), .B(j_k_ff_3_q), .A(j_k_ff_4_q), .a_2(a), .b_2(b), .c_2(c), .d_2(d),
    .e(e), .f(f), .g(g));
  J_K_Flip_Flop #(.trigger("falling")) j_k_ff_4 (
    .J(1'b1), .clk(j_k_ff_3_q), .K(1'b1), .Q(j_k_ff_4_q), .reset(or_1_out));  // open: Qn, preset, en

  // Notes on the sheet:
  //   D
  //   C
  //   B
  //   A
endmodule
