// Logisim project main.circ as structural Verilog: 1 circuit, main circuit main
module main (
);

  wire contador_2_horas_1_a, contador_2_horas_1_b, contador_2_horas_1_c, contador_2_horas_1_d,
       contador_2_horas_1_e, contador_2_horas_1_f, contador_2_horas_1_g, contador_6_minutos_1_a,
       contador_6_minutos_1_b, contador_6_minutos_1_c, contador_6_minutos_1_d, contador_6_minutos_1_e,
       contador_6_minutos_1_f, contador_6_minutos_1_g, contador_6_segundos_1_a, contador_6_segundos_1_b,
       contador_6_segundos_1_c, contador_6_segundos_1_d, contador_6_segundos_1_e, contador_6_segundos_1_f,
       contador_6_segundos_1_g, contador_9_minutos_1_a, contador_9_minutos_1_b, contador_9_minutos_1_c,
       contador_9_minutos_1_d, contador_9_minutos_1_e, contador_9_minutos_1_f, contador_9_minutos_1_g,
       contador_9_segundos_1_a, contador_9_segundos_1_b, contador_9_segundos_1_c, contador_9_segundos_1_d,
       contador_9_segundos_1_e, contador_9_segundos_1_f, contador_9_segundos_1_g, contador_horas_unidade_1_a,
       contador_horas_unidade_1_b, contador_horas_unidade_1_c, contador_horas_unidade_1_d,
       contador_horas_unidade_1_e, contador_horas_unidade_1_f, contador_horas_unidade_1_g;

  _7_Segment_Display u_7_segment_display_1 (
    .g(contador_2_horas_1_a), .f(contador_2_horas_1_b), .a(contador_2_horas_1_c), .b(contador_2_horas_1_d),
    .e(contador_2_horas_1_e), .d(contador_2_horas_1_f), .c(contador_2_horas_1_g));  // open: dp
  Contador_2_Horas contador_2_horas_1 (
    .a(contador_2_horas_1_a), .b(contador_2_horas_1_b), .c(contador_2_horas_1_c), .d(contador_2_horas_1_d),
    .e(contador_2_horas_1_e), .f(contador_2_horas_1_f), .g(contador_2_horas_1_g));  // open: reset, _24
  _7_Segment_Display u_7_segment_display_2 (
    .g(contador_horas_unidade_1_a), .f(contador_horas_unidade_1_b), .a(contador_horas_unidade_1_c),
    .b(contador_horas_unidade_1_d), .e(contador_horas_unidade_1_e), .d(contador_horas_unidade_1_f),
    .c(contador_horas_unidade_1_g));  // open: dp
  Contador_Horas_Unidade contador_horas_unidade_1 (
    .a(contador_horas_unidade_1_a), .b(contador_horas_unidade_1_b), .c(contador_horas_unidade_1_c),
    .d(contador_horas_unidade_1_d), .e(contador_horas_unidade_1_e), .f(contador_horas_unidade_1_f),
    .g(contador_horas_unidade_1_g));  // open: reset
  _7_Segment_Display u_7_segment_display_3 (
    .g(contador_6_minutos_1_a), .f(contador_6_minutos_1_b), .a(contador_6_minutos_1_c),
    .b(contador_6_minutos_1_d), .e(contador_6_minutos_1_e), .d(contador_6_minutos_1_f),
    .c(contador_6_minutos_1_g));  // open: dp
  Contador_6_Minutos contador_6_minutos_1 (
    .a(contador_6_minutos_1_a), .b(contador_6_minutos_1_b), .c(contador_6_minutos_1_c),
    .d(contador_6_minutos_1_d), .e(contador_6_minutos_1_e), .f(contador_6_minutos_1_f),
    .g(contador_6_minutos_1_g));  // open: reset
  _7_Segment_Display u_7_segment_display_4 (
    .g(contador_9_minutos_1_a), .f(contador_9_minutos_1_b), .a(contador_9_minutos_1_c),
    .b(contador_9_minutos_1_d), .e(contador_9_minutos_1_e), .d(contador_9_minutos_1_f),
    .c(contador_9_minutos_1_g));  // open: dp
  Contador_9_Minutos contador_9_minutos_1 (
    .a(contador_9_minutos_1_a), .b(contador_9_minutos_1_b), .c(contador_9_minutos_1_c),
    .d(contador_9_minutos_1_d), .e(contador_9_minutos_1_e), .f(contador_9_minutos_1_f),
    .g(contador_9_minutos_1_g));  // open: reset
  _7_Segment_Display u_7_segment_display_5 (
    .g(contador_6_segundos_1_a), .f(contador_6_segundos_1_b), .a(contador_6_segundos_1_c),
    .b(contador_6_segundos_1_d), .e(contador_6_segundos_1_e), .d(contador_6_segundos_1_f),
    .c(contador_6_segundos_1_g));  // open: dp
  Contador_6_Segundos contador_6_segundos_1 (
    .a(contador_6_segundos_1_a), .b(contador_6_segundos_1_b), .c(contador_6_segundos_1_c),
    .d(contador_6_segundos_1_d), .e(contador_6_segundos_1_e), .f(contador_6_segundos_1_f),
    .g(contador_6_segundos_1_g));  // open: reset
  _7_Segment_Display u_7_segment_display_6 (
    .g(contador_9_segundos_1_a), .f(contador_9_segundos_1_b), .a(contador_9_segundos_1_c),
    .b(contador_9_segundos_1_d), .e(contador_9_segundos_1_e), .d(contador_9_segundos_1_f),
    .c(contador_9_segundos_1_g));  // open: dp
  Contador_9_Segundos contador_9_segundos_1 (
    .a(contador_9_segundos_1_a), .b(contador_9_segundos_1_b), .c(contador_9_segundos_1_c),
    .d(contador_9_segundos_1_d), .e(contador_9_segundos_1_e), .f(contador_9_segundos_1_f),
    .g(contador_9_segundos_1_g));  // open: reset

  // Notes on the sheet:
  //   :
  //   :
endmodule
